# Fritzing sketch FrtizingProject (saved by Fritzing 0.9.3b)
breadboards: 1

parts:
  Part1 = Arduino Uno (Rev3)
  U1 = POT_SWITCH [package=pot_pth]
  U2 = SN74LS32N [package="DIP14 [THT]"]

nets:
  N1: Part1.A3, U1.G$2_1
  N2: Part1.D9_PWM, U2.1A, U2.2A, U2.4B
  N3: Part1.D3_PWM, U2.4A
  N4: Part1.D5_PWM, U2.1B
  N5: Part1.D7, U2.2B
  5V: Part1.5V, U1.G$1_A, U2.Vcc
  GND: Part1.GND, U1.G$1_E, U2.GND

notes:
  2 LS_U - 4 LS_V -
  6 LS_W
  3 HS_U - 5 HS_V -
  7 HS_W
  hall sensors.
  A0 yellow - A1 green -A2 blue
